# Fritzing sketch huzzah_adc_temp (saved by Fritzing 0.9.2b)
circuit board: 7cm x 5cm
breadboards: 2

parts:
  Composant1 = HUZZAH ESP8266 Breakout  # not connected
  U1 = Voltage Regulator [package=to220-adj]
  IC1 = MCP3008 8-channel 10-bit ADC [part_number=MCP3008]
  DS1 = DS18B20 1-Wire Temperature Sensor [part_number=DS18B20]  # not connected
  R1 = Resistor [tolerance=±5% resistance=150 package=THT]
  C1 = Ceramic Capacitor [capacitance=0.1µF package="100 mil [THT, multilayer]"]
  C2 = Electrolytic Capacitor [capacitance=10µF package="100 mil [THT, electrolytic]"]
  R2 = Resistor [tolerance=±5% resistance=150 package=THT]
  R3 = Resistor [tolerance=±5% resistance=150 package=THT]
  R4 = Resistor [tolerance=±5% resistance=150 package=THT]
  JACK1 = 2.1mm DC Barrel Jack

nets:
  N1: U1.ADJ, R1.Pin_0, R4.Pin_1
  N2: U1.IN, R2.Pin_0
  N3: U1.OUT, C1.1, JACK1.center
  N4: IC1.no_name_yet#5, IC1.no_name_yet#11, IC1.no_name_yet#12
  N5: R1.Pin_1, C1.0, C2.-, JACK1.sleeve
  N6: R2.Pin_1, R3.Pin_1
  N7: R3.Pin_0, R4.Pin_0

custom parts:
  HUZZAH ESP8266 Breakout: The ESP8266 processor from Espressif is an 80 MHz microcontroller with a full WiFi front-end (both as client and access point) and TCP/IP stack with DNS support as well.
  2.1mm DC Barrel Jack: 2.1mm DC Barrel Jack with Thru-Hole Connectors (breadboardable)
